// Logisim project RISC-V SINGLE CYCLE.circ as structural Verilog
module type_decode (
  input  [6:0] in_1,
  output R_formate,
  output I_TYPE,
  output LOAD,
  output STORE,
  output BRANCH,
  output JAL,
  output JALR,
  output LUI,
  output AUIPC
);

  Comparator #(.width(7)) comparator_1 (.a(in_1), .b(7'b0110011), .eq(R_formate));  // open: gt, lt
  Comparator #(.width(7)) comparator_2 (.a(in_1), .b(7'b0010011), .eq(I_TYPE));  // open: gt, lt
  Comparator #(.width(7)) comparator_3 (.a(in_1), .b(7'b0000011), .eq(LOAD));  // open: gt, lt
  Comparator #(.width(7)) comparator_4 (.a(in_1), .b(7'b0100011), .eq(STORE));  // open: gt, lt
  Comparator #(.width(7)) comparator_5 (.a(in_1), .b(7'b1100011), .eq(BRANCH));  // open: gt, lt
  Comparator #(.width(7)) comparator_6 (.a(in_1), .b(7'b1101111), .eq(JAL));  // open: gt, lt
  Comparator #(.width(7)) comparator_7 (.a(in_1), .b(7'b1100111), .eq(JALR));  // open: gt, lt
  Comparator #(.width(7)) comparator_8 (.a(in_1), .b(7'b0110111), .eq(LUI));  // open: gt, lt
  Comparator #(.width(7)) comparator_9 (.a(in_1), .b(7'b0010111), .eq(AUIPC));  // open: gt, lt
endmodule

module immediate_generation (
  input  [31:0] in_1,
  input  [31:0] in_2,
  output [31:0] out_3,
  output [31:0] out_4,
  output [31:0] out_5,
  output [31:0] out_6,
  output [31:0] out_7
);

  wire [19:0] shifter_1_out;
  wire [31:0] bit_extender_3_out, bit_extender_4_out;

  Shifter #(.width(20)) shifter_1 (.in(in_2[31:12]), .\dist (5'b01100), .out(shifter_1_out));
  assign out_3 = {{20{in_2[31]}}, in_2[31:20]};  // Bit_Extender bit_extender_1
  assign out_4 = {{20{in_2[31]}}, {in_2[31:25], in_2[11:7]}};  // Bit_Extender bit_extender_2
  assign bit_extender_3_out = {{19{in_2[31]}}, {in_2[31], in_2[7], in_2[30:25], in_2[11:8], 1'b0}};  // Bit_Extender bit_extender_3
  assign bit_extender_4_out = {{11{in_2[31]}}, {in_2[31], in_2[19:12], in_2[20], in_2[30:21], 1'b0}};  // Bit_Extender bit_extender_4
  assign out_7 = {{12{shifter_1_out[19]}}, shifter_1_out};  // Bit_Extender bit_extender_5
  Adder #(.width(32)) adder_1 (.a(bit_extender_3_out), .b(in_1), .out(out_5));  // open: cin, cout
  Adder #(.width(32)) adder_2 (.a(bit_extender_4_out), .b(in_1), .out(out_6));  // open: cin, cout

  // Notes on the sheet:
  //   PC
  //   INSTRUCTION
  //   I-TYPE
  //   S-TYPE
  //   SB-TYPE
  //   UJ-TYE
  //   U-TYPE
endmodule

module pc (
  input  in_1
);

  wire clock_1_out;
  wire [31:0] adder_1_out, register_1_q;

  Register #(.width(32)) register_1 (.D(adder_1_out), .Q(register_1_q), .clk(clock_1_out), .clr(in_1));  // open: en
  Clock clock_1 (.out(clock_1_out));
  Adder #(.width(32)) adder_1 (.a(register_1_q), .b(32'h4), .out(adder_1_out));  // open: cin, cout
  ROM #(.addrWidth(12)) rom_1 (.addr(register_1_q[13:2]));  // open: data, sel

  // Notes on the sheet:
  //   contents of rom_1 (hex, n*v repeats v):
  //   30 13
endmodule

module register_file_circ (
  input  [31:0] in_1,
  input  [4:0] in_2,
  input  in_3,
  input  [4:0] in_4,
  input  [4:0] in_5,
  input  in_6,
  output [31:0] out_7,
  output [31:0] out_8
);

  wire decoder_1_out0, decoder_1_out1, decoder_1_out2, decoder_1_out3, decoder_1_out4, decoder_1_out5,
       decoder_1_out6, decoder_1_out7, decoder_1_out8, decoder_1_out9, decoder_1_out10, decoder_1_out11,
       decoder_1_out12, decoder_1_out13, decoder_1_out14, decoder_1_out15, decoder_1_out16, decoder_1_out17,
       decoder_1_out18, decoder_1_out19, decoder_1_out20, decoder_1_out21, decoder_1_out22, decoder_1_out23,
       decoder_1_out24, decoder_1_out25, decoder_1_out26, decoder_1_out27, decoder_1_out28, decoder_1_out29,
       decoder_1_out30, decoder_1_out31, undriven;
  wire [31:0] register_1_q, register_2_q, register_3_q, register_4_q, register_5_q, register_6_q,
       register_7_q, register_8_q, register_9_q, register_10_q, register_11_q, register_12_q, register_13_q,
       register_14_q, register_15_q, register_16_q, register_17_q, register_18_q, register_19_q,
       register_20_q, register_21_q, register_22_q, register_23_q, register_24_q, register_25_q,
       register_26_q, register_27_q, register_28_q, register_29_q, register_30_q, register_31_q,
       register_32_q;

  Decoder #(.select(5)) decoder_1 (
    .out0(decoder_1_out0), .out1(decoder_1_out1), .out2(decoder_1_out2), .out3(decoder_1_out3),
    .out4(decoder_1_out4), .out5(decoder_1_out5), .out6(decoder_1_out6), .out7(decoder_1_out7),
    .out8(decoder_1_out8), .out9(decoder_1_out9), .out10(decoder_1_out10), .out11(decoder_1_out11),
    .out12(decoder_1_out12), .out13(decoder_1_out13), .out14(decoder_1_out14), .out15(decoder_1_out15),
    .out16(decoder_1_out16), .out17(decoder_1_out17), .out18(decoder_1_out18), .out19(decoder_1_out19),
    .out20(decoder_1_out20), .out21(decoder_1_out21), .out22(decoder_1_out22), .out23(decoder_1_out23),
    .out24(decoder_1_out24), .out25(decoder_1_out25), .out26(decoder_1_out26), .out27(decoder_1_out27),
    .out28(decoder_1_out28), .out29(decoder_1_out29), .out30(decoder_1_out30), .out31(decoder_1_out31),
    .sel(in_5), .en(in_3));
  Register #(.width(32)) register_1 (.D({32{1'b0}}), .en(decoder_1_out0), .Q(register_1_q), .clk(in_6));  // open: clr
  Register #(.width(32)) register_2 (.D(in_1), .en(decoder_1_out1), .Q(register_2_q), .clk(in_6));  // open: clr
  Register #(.width(32)) register_3 (.D(in_1), .en(decoder_1_out2), .Q(register_3_q), .clk(in_6));  // open: clr
  Register #(.width(32)) register_4 (.D(in_1), .en(decoder_1_out3), .Q(register_4_q), .clk(in_6));  // open: clr
  Register #(.width(32)) register_5 (.D(in_1), .en(decoder_1_out4), .Q(register_5_q), .clk(in_6));  // open: clr
  Register #(.width(32)) register_6 (.D(in_1), .en(decoder_1_out5), .Q(register_6_q), .clk(in_6));  // open: clr
  Register #(.width(32)) register_7 (.D(in_1), .en(decoder_1_out6), .Q(register_7_q), .clk(in_6));  // open: clr
  Register #(.width(32)) register_8 (.D(in_1), .en(decoder_1_out7), .Q(register_8_q), .clk(in_6));  // open: clr
  Register #(.width(32)) register_9 (.D(in_1), .en(decoder_1_out8), .Q(register_9_q), .clk(in_6));  // open: clr
  Register #(.width(32)) register_10 (.D(in_1), .en(decoder_1_out9), .Q(register_10_q), .clk(in_6));  // open: clr
  Register #(.width(32)) register_11 (.D(in_1), .en(decoder_1_out10), .Q(register_11_q), .clk(in_6));  // open: clr
  Register #(.width(32)) register_12 (.D(in_1), .en(decoder_1_out11), .Q(register_12_q), .clk(in_6));  // open: clr
  Register #(.width(32)) register_13 (.D(in_1), .en(decoder_1_out12), .Q(register_13_q), .clk(in_6));  // open: clr
  Register #(.width(32)) register_14 (.D(in_1), .en(decoder_1_out13), .Q(register_14_q), .clk(in_6));  // open: clr
  Register #(.width(32)) register_15 (.D(in_1), .en(decoder_1_out14), .Q(register_15_q), .clk(in_6));  // open: clr
  Register #(.width(32)) register_16 (.D(in_1), .en(decoder_1_out15), .Q(register_16_q), .clk(in_6));  // open: clr
  Register #(.width(32)) register_17 (.D(in_1), .en(decoder_1_out16), .Q(register_17_q), .clk(in_6));  // open: clr
  Register #(.width(32)) register_18 (.D(in_1), .en(decoder_1_out17), .Q(register_18_q), .clk(in_6));  // open: clr
  Register #(.width(32)) register_19 (.D(in_1), .en(decoder_1_out18), .Q(register_19_q), .clk(in_6));  // open: clr
  Register #(.width(32)) register_20 (.D(in_1), .en(decoder_1_out19), .Q(register_20_q), .clk(in_6));  // open: clr
  Register #(.width(32)) register_21 (.D(in_1), .en(decoder_1_out20), .Q(register_21_q), .clk(in_6));  // open: clr
  Register #(.width(32)) register_22 (.D(in_1), .en(decoder_1_out21), .Q(register_22_q), .clk(in_6));  // open: clr
  Register #(.width(32)) register_23 (.D(in_1), .en(decoder_1_out22), .Q(register_23_q), .clk(in_6));  // open: clr
  Register #(.width(32)) register_24 (.D(in_1), .en(decoder_1_out23), .Q(register_24_q), .clk(in_6));  // open: clr
  Register #(.width(32)) register_25 (.D(in_1), .en(decoder_1_out24), .Q(register_25_q), .clk(in_6));  // open: clr
  Register #(.width(32)) register_26 (.D(in_1), .en(decoder_1_out25), .Q(register_26_q), .clk(in_6));  // open: clr
  Register #(.width(32)) register_27 (.D(in_1), .en(decoder_1_out26), .Q(register_27_q), .clk(in_6));  // open: clr
  Register #(.width(32)) register_28 (.D(in_1), .en(decoder_1_out27), .Q(register_28_q), .clk(in_6));  // open: clr
  Register #(.width(32)) register_29 (.D(in_1), .en(decoder_1_out28), .Q(register_29_q), .clk(in_6));  // open: clr
  Register #(.width(32)) register_30 (.D(in_1), .en(decoder_1_out29), .Q(register_30_q), .clk(in_6));  // open: clr
  Register #(.width(32)) register_31 (.D(in_1), .en(decoder_1_out30), .Q(register_31_q), .clk(in_6));  // open: clr
  Register #(.width(32)) register_32 (.D(in_1), .en(decoder_1_out31), .Q(register_32_q), .clk(in_6));  // open: clr
  Multiplexer #(.select(5), .width(32)) multiplexer_1 (
    .in0(register_1_q), .in1(register_2_q), .in2(register_3_q), .in3(register_4_q), .in4(register_5_q),
    .in5(register_6_q), .in6(register_7_q), .in7(register_8_q), .in8(register_9_q), .in9(register_10_q),
    .in10(register_11_q), .in11(register_12_q), .in12(register_13_q), .in13(register_14_q),
    .in14(register_15_q), .in15(register_16_q), .in16(register_17_q), .in17(register_18_q),
    .in18(register_19_q), .in19(register_20_q), .in20(register_21_q), .in21(register_22_q),
    .in22(register_23_q), .in23(register_24_q), .in24(register_25_q), .in25(register_26_q),
    .in26(register_27_q), .in27(register_28_q), .in28(register_29_q), .in29(register_30_q),
    .in30(register_31_q), .in31(register_32_q), .out(out_7), .sel(in_2), .en(undriven));
  Multiplexer #(.select(5), .width(32)) multiplexer_2 (
    .in0(register_1_q), .in1(register_2_q), .in2(register_3_q), .in3(register_4_q), .in4(register_5_q),
    .in5(register_6_q), .in6(register_7_q), .in7(register_8_q), .in8(register_9_q), .in9(register_10_q),
    .in10(register_11_q), .in11(register_12_q), .in12(register_13_q), .in13(register_14_q),
    .in14(register_15_q), .in15(register_16_q), .in16(register_17_q), .in17(register_18_q),
    .in18(register_19_q), .in19(register_20_q), .in20(register_21_q), .in21(register_22_q),
    .in22(register_23_q), .in23(register_24_q), .in24(register_25_q), .in25(register_26_q),
    .in26(register_27_q), .in27(register_28_q), .in28(register_29_q), .in29(register_30_q),
    .in30(register_31_q), .in31(register_32_q), .out(out_8), .sel(in_4));  // open: en
endmodule

module control_decode (
  input  I_type,
  input  Load,
  input  in_3,
  input  Store,
  input  Branch,
  input  jal,
  input  jalr,
  input  lui,
  input  Auipc,
  input  [2:0] in_10,
  input  in_11,
  output REG_WRITE,
  output mem_to_reg,
  output MEM_WRITE,
  output BRANCH_2,
  output [1:0] OPERAND_A,
  output OPERAND_B,
  output [1:0] NEXT_PC,
  output [3:0] out_19,
  output [1:0] out_20
);

  wire alu_op_1_a, alu_op_1_b, alu_op_1_c, or_1_out, or_2_out;

  or or_1 (or_1_out, Auipc, lui);
  or or_2 (or_2_out, jalr, in_3, Load);
  or or_3 (REG_WRITE, I_type, Load, in_3, Auipc, jal, jalr, lui);
  operand_A_circ operand_a_circ_1 (
    .AUIPC(Auipc), .JAL(jal), .JALR(jalr), .LUI(lui), .a(OPERAND_A[0]), .b(OPERAND_A[1]));  // open: RS1
  or or_4 (OPERAND_B, Auipc, Store, lui, Branch, Load);
  NEXT_PC next_pc_1 (.jal(Branch), .jalr(jal), .BRANCH(jalr), .a(NEXT_PC[0]), .b(NEXT_PC[1]));
  alu_op alu_op_1 (
    .R_TYPE(I_type), .I_TYPE(Load), .LOAD(in_3), .STORE(Store), .JAL(jal), .JALR(jalr), .LUI(lui),
    .AUIPC(Auipc), .a(alu_op_1_a), .b(alu_op_1_b), .c(alu_op_1_c));
  imm_sel imm_sel_1 (.store(Store), .u_tye(or_1_out), .I_type(or_2_out), .a(out_20[0]), .b(out_20[1]));
  alu_controller alu_controller_1 (
    .ALU_OP_1(alu_op_1_a), .ALU_OP_2(alu_op_1_b), .ALU_OP_3(alu_op_1_c), .FUNC_3_1(in_10[0]),
    .FUNC_3_2(in_10[1]), .FUNC_3_3(in_10[2]), .FUNC_7(in_11), .a(out_19[3]), .b(out_19[2]), .c(out_19[1]),
    .d(out_19[0]));

  assign BRANCH_2 = Branch;
  assign mem_to_reg = in_3;
  assign MEM_WRITE = Store;

  // Notes on the sheet:
  //   R-type
  //   Immegiate-selector
  //   ALU_CONTROL
endmodule

module NEXT_PC (
  input  jal,
  input  jalr,
  input  BRANCH,
  output a,
  output b
);

  or or_1 (a, BRANCH, jalr);
  or or_2 (b, BRANCH, jal);
endmodule

module alu_op (
  input  R_TYPE,
  input  I_TYPE,
  input  LOAD,
  input  STORE,
  input  JAL,
  input  JALR,
  input  LUI,
  input  AUIPC,
  output a,
  output b,
  output c
);

  or or_1 (a, AUIPC, LUI, JALR, JAL);
  or or_2 (b, AUIPC, LUI, STORE, LOAD);
  or or_3 (c, AUIPC, JALR, STORE, I_TYPE);
endmodule

module imm_sel (
  input  store,
  input  u_tye,
  input  I_type,
  output a,
  output b
);

  or or_1 (a, u_tye, store);
  or or_2 (b, I_type, store);
endmodule

module alu_controller (
  input  ALU_OP_1,
  input  ALU_OP_2,
  input  ALU_OP_3,
  input  FUNC_3_1,
  input  FUNC_3_2,
  input  FUNC_3_3,
  input  FUNC_7,
  output a,
  output b,
  output c,
  output d
);

  wire and_1_out, and_2_out, and_3_out, and_4_out, and_5_out, and_6_out, and_7_out, and_8_out, and_9_out,
       and_10_out, and_11_out, and_12_out, and_13_out, and_14_out, and_15_out, and_16_out, and_17_out,
       not_1_out, not_2_out, not_3_out, not_4_out, not_5_out, not_6_out, not_7_out, not_8_out, not_9_out,
       not_10_out, not_11_out, not_12_out, not_13_out, not_14_out, not_15_out, not_16_out, not_17_out,
       not_18_out, not_19_out, not_20_out, not_21_out, not_22_out, not_23_out, not_24_out, not_25_out,
       not_26_out, not_27_out, not_28_out, not_29_out, not_30_out, not_31_out, not_32_out, not_33_out,
       not_34_out;

  not not_1 (not_1_out, ALU_OP_1);
  not not_2 (not_2_out, FUNC_3_2);
  not not_3 (not_3_out, ALU_OP_1);
  not not_4 (not_4_out, FUNC_3_1);
  not not_5 (not_5_out, ALU_OP_2);
  not not_6 (not_6_out, ALU_OP_1);
  not not_7 (not_7_out, FUNC_3_1);
  not not_8 (not_8_out, FUNC_3_2);
  not not_9 (not_9_out, ALU_OP_2);
  not not_10 (not_10_out, FUNC_3_1);
  not not_11 (not_11_out, FUNC_3_3);
  not not_12 (not_12_out, ALU_OP_1);
  not not_13 (not_13_out, FUNC_3_2);
  not not_14 (not_14_out, FUNC_3_3);
  not not_15 (not_15_out, ALU_OP_1);
  not not_16 (not_16_out, FUNC_3_2);
  not not_17 (not_17_out, FUNC_7);
  not not_18 (not_18_out, ALU_OP_2);
  not not_19 (not_19_out, ALU_OP_2);
  not not_20 (not_20_out, FUNC_3_3);
  not not_21 (not_21_out, ALU_OP_1);
  not not_22 (not_22_out, FUNC_7);
  not not_23 (not_23_out, ALU_OP_2);
  not not_24 (not_24_out, ALU_OP_2);
  not not_25 (not_25_out, ALU_OP_2);
  not not_26 (not_26_out, ALU_OP_3);
  not not_27 (not_27_out, ALU_OP_1);
  not not_28 (not_28_out, FUNC_3_1);
  not not_29 (not_29_out, FUNC_3_2);
  not not_30 (not_30_out, ALU_OP_1);
  not not_31 (not_31_out, FUNC_3_2);
  not not_32 (not_32_out, ALU_OP_2);
  not not_33 (not_33_out, FUNC_3_3);
  not not_34 (not_34_out, ALU_OP_2);
  and and_1 (and_1_out, not_1_out, not_2_out, FUNC_3_3, FUNC_7);
  and and_2 (and_2_out, not_3_out, not_4_out, FUNC_3_2, FUNC_3_3);
  and and_3 (and_3_out, ALU_OP_1, not_5_out);
  and and_4 (and_4_out, not_6_out, not_7_out, not_8_out, FUNC_3_3);
  and and_5 (and_5_out, not_9_out, not_10_out, FUNC_3_2, not_11_out);
  and and_6 (and_6_out, not_12_out, FUNC_3_1, not_13_out, not_14_out);
  and and_7 (and_7_out, not_15_out, FUNC_3_1, not_16_out, not_17_out);
  and and_8 (and_8_out, ALU_OP_1, not_18_out);
  and and_9 (and_9_out, not_19_out, FUNC_3_2, not_20_out);
  and and_10 (and_10_out, not_21_out, FUNC_3_1, FUNC_3_3, not_22_out);
  and and_11 (and_11_out, not_23_out, FUNC_3_1, FUNC_3_2);
  and and_12 (and_12_out, ALU_OP_1, not_24_out);
  and and_13 (and_13_out, not_25_out, not_26_out, FUNC_7);
  and and_14 (and_14_out, not_27_out, not_28_out, not_29_out, FUNC_3_3);
  and and_15 (and_15_out, not_30_out, not_31_out, FUNC_3_3, FUNC_7);
  and and_16 (and_16_out, not_32_out, FUNC_3_2, not_33_out);
  and and_17 (and_17_out, ALU_OP_1, not_34_out);
  or or_1 (a, and_1_out, and_2_out, and_3_out);
  or or_2 (b, and_4_out, and_5_out, and_6_out, and_7_out, and_8_out);
  or or_3 (c, and_9_out, and_10_out, and_11_out, and_12_out);
  or or_4 (d, and_13_out, and_14_out, and_15_out, and_16_out, and_17_out);
endmodule

module alu (
  input  [31:0] in_1,
  input  [31:0] in_2,
  input  [3:0] in_3,
  output [31:0] out_4
);

  wire comparator_1_lt, comparator_2_lt;
  wire [31:0] adder_1_out, and_1_out, bit_extender_1_out, bit_extender_2_out, or_1_out, shifter_1_out,
       shifter_2_out, shifter_3_out, subtractor_1_out, xor_1_out;

  Adder #(.width(32)) adder_1 (.a(in_2), .b(in_1), .out(adder_1_out));  // open: cin, cout
  Subtractor #(.width(32)) subtractor_1 (.a(in_2), .b(in_1), .out(subtractor_1_out));  // open: bin, bout
  assign and_1_out = in_2 & in_1;  // AND_Gate and_1, 32 bits wide
  assign or_1_out = in_2 | in_1;  // OR_Gate or_1, 32 bits wide
  assign xor_1_out = in_2 ^ in_1;  // XOR_Gate xor_1, 32 bits wide
  Shifter #(.width(32)) shifter_1 (.in(in_2), .\dist (in_1[4:0]), .out(shifter_1_out));
  Shifter #(.width(32), .shift("lr")) shifter_2 (.in(in_2), .\dist (in_1[4:0]), .out(shifter_2_out));
  Comparator #(.width(32)) comparator_1 (.a(in_2), .b(in_1), .lt(comparator_1_lt));  // open: gt, eq
  Comparator #(.width(32)) comparator_2 (.a(in_2), .b(in_1), .lt(comparator_2_lt));  // open: gt, eq
  Shifter #(.width(32), .shift("ar")) shifter_3 (.in(in_2), .\dist (in_1[4:0]), .out(shifter_3_out));
  assign bit_extender_1_out = {{31{1'b0}}, comparator_2_lt};  // Bit_Extender bit_extender_1
  assign bit_extender_2_out = {{31{comparator_1_lt}}, comparator_1_lt};  // Bit_Extender bit_extender_2
  Multiplexer #(.select(4), .width(32), .enable("false")) multiplexer_1 (
    .in0(adder_1_out), .in1(subtractor_1_out), .in2(and_1_out), .in3(or_1_out), .in4(xor_1_out),
    .in5(shifter_1_out), .in6(shifter_2_out), .in7(bit_extender_2_out), .in8(bit_extender_1_out),
    .in9(shifter_3_out), .in15(in_2), .out(out_4), .sel(in_3));  // open: in10, in11, in12, in13, in14

  // Notes on the sheet:
  //   OPERAND_A
  //   OPERAND_B
endmodule

module control_unit (
  input  [6:0] OPCODE,
  input  [2:0] in_2,
  input  in_3,
  output out_4,
  output out_5,
  output out_6,
  output out_7,
  output [1:0] out_8,
  output out_9,
  output [1:0] out_10,
  output [3:0] out_11,
  output [1:0] out_12
);

  wire TYPE_DECODER_auipc, TYPE_DECODER_branch, TYPE_DECODER_i_type, TYPE_DECODER_jal, TYPE_DECODER_jalr,
       TYPE_DECODER_load, TYPE_DECODER_lui, TYPE_DECODER_r_formate, TYPE_DECODER_store;

  type_decode TYPE_DECODER (
    .in_1(OPCODE), .R_formate(TYPE_DECODER_r_formate), .LOAD(TYPE_DECODER_load), .STORE(TYPE_DECODER_store),
    .BRANCH(TYPE_DECODER_branch), .JALR(TYPE_DECODER_jalr), .JAL(TYPE_DECODER_jal), .LUI(TYPE_DECODER_lui),
    .AUIPC(TYPE_DECODER_auipc), .I_TYPE(TYPE_DECODER_i_type));
  control_decode control_decode_1 (
    .I_type(TYPE_DECODER_r_formate), .Load(TYPE_DECODER_i_type), .in_3(TYPE_DECODER_load),
    .Store(TYPE_DECODER_store), .Branch(TYPE_DECODER_branch), .jal(TYPE_DECODER_jal),
    .jalr(TYPE_DECODER_jalr), .lui(TYPE_DECODER_lui), .Auipc(TYPE_DECODER_auipc), .REG_WRITE(out_4),
    .mem_to_reg(out_5), .MEM_WRITE(out_6), .BRANCH_2(out_7), .OPERAND_A(out_8), .OPERAND_B(out_9),
    .NEXT_PC(out_10), .out_20(out_12), .in_11(in_3), .in_10({in_2[0], in_2[1], in_2[2]}), .out_19(out_11));
endmodule

module branch (
  input  [31:0] in_1,
  input  [31:0] in_2,
  input  [2:0] in_3,
  input  in_4,
  output out_5
);

  wire comparator_1_eq, comparator_2_eq, comparator_3_lt, comparator_4_eq, comparator_4_gt, comparator_5_lt,
       comparator_6_eq, comparator_6_gt, not_1_out, or_1_out, or_2_out;

  Comparator #(.width(32)) comparator_1 (.a(in_1), .b(in_2), .eq(comparator_1_eq));  // open: gt, lt
  Comparator #(.width(32)) comparator_2 (.a(in_1), .b(in_2), .eq(comparator_2_eq));  // open: gt, lt
  Comparator #(.width(32)) comparator_3 (.a(in_1), .b(in_2), .lt(comparator_3_lt));  // open: gt, eq
  Comparator #(.width(32)) comparator_4 (.a(in_1), .b(in_2), .gt(comparator_4_gt), .eq(comparator_4_eq));  // open: lt
  Comparator #(.width(32), .mode("unsigned")) comparator_5 (.a(in_1), .b(in_2), .lt(comparator_5_lt));  // open: gt, eq
  Comparator #(.width(32), .mode("unsigned")) comparator_6 (
    .a(in_1), .b(in_2), .gt(comparator_6_gt), .eq(comparator_6_eq));  // open: lt
  not not_1 (not_1_out, comparator_2_eq);
  or or_1 (or_1_out, comparator_4_gt, comparator_4_eq);
  or or_2 (or_2_out, comparator_6_gt, comparator_6_eq);
  Multiplexer #(.select(3)) multiplexer_1 (
    .in0(comparator_1_eq), .in1(not_1_out), .in4(comparator_3_lt), .in5(or_1_out), .in6(comparator_5_lt),
    .in7(or_2_out), .out(out_5), .sel(in_3), .en(in_4));  // open: in2, in3

  // Notes on the sheet:
  //   A
  //   B
endmodule

module rv32i_microprocessor (
  input  RESET
);

  wire a_out_5, clock_1_out, control_unit_1_out_4, control_unit_1_out_5, control_unit_1_out_6,
       control_unit_1_out_7, control_unit_1_out_9;
  wire [1:0] control_unit_1_out_8, control_unit_1_out_10, control_unit_1_out_12;
  wire [3:0] control_unit_1_out_11;
  wire [11:0] alu_1_out_4_2;
  wire [31:0] adder_1_out, adder_2_out, alu_1_out_4, immediate_generation_1_out_3,
       immediate_generation_1_out_4, immediate_generation_1_out_5, immediate_generation_1_out_6,
       immediate_generation_1_out_7, multiplexer_1_out, multiplexer_2_out, multiplexer_3_out,
       multiplexer_4_out, multiplexer_5_out, multiplexer_6_out, ram_1_data, register_1_q,
       register_file_circ_1_out_7, register_file_circ_1_out_8, rom_1_data;

  Adder #(.width(32)) adder_1 (
    .a(register_file_circ_1_out_7), .b(immediate_generation_1_out_3), .out(adder_1_out));  // open: cin, cout
  Multiplexer #(.select(2), .width(32)) multiplexer_1 (
    .in0(adder_2_out), .in1(immediate_generation_1_out_6), .in2(multiplexer_2_out), .in3(adder_1_out),
    .out(multiplexer_1_out), .sel(control_unit_1_out_10));  // open: en
  Register #(.width(32)) register_1 (
    .D(multiplexer_1_out), .Q(register_1_q), .clk(clock_1_out), .clr(RESET));  // open: en
  register_file_circ register_file_circ_1 (
    .in_1(multiplexer_6_out), .in_2(rom_1_data[19:15]), .in_3(control_unit_1_out_4),
    .in_4(rom_1_data[24:20]), .in_5(rom_1_data[11:7]), .out_7(register_file_circ_1_out_7),
    .out_8(register_file_circ_1_out_8), .in_6(clock_1_out));
  Multiplexer #(.width(32)) multiplexer_2 (
    .in0(adder_2_out), .in1(immediate_generation_1_out_5), .out(multiplexer_2_out), .sel(a_out_5));  // open: en
  Adder #(.width(32)) adder_2 (.a(register_1_q), .b(32'h4), .out(adder_2_out));  // open: cin, cout
  immediate_generation immediate_generation_1 (
    .in_1(register_1_q), .in_2(rom_1_data), .out_3(immediate_generation_1_out_3),
    .out_4(immediate_generation_1_out_4), .out_5(immediate_generation_1_out_5),
    .out_6(immediate_generation_1_out_6), .out_7(immediate_generation_1_out_7));
  ROM #(.addrWidth(12), .dataWidth(32)) rom_1 (.addr(register_1_q[13:2]), .data(rom_1_data));  // open: sel
  Clock clock_1 (.out(clock_1_out));
  control_unit control_unit_1 (
    .OPCODE(rom_1_data[6:0]), .out_4(control_unit_1_out_4), .out_5(control_unit_1_out_5),
    .out_6(control_unit_1_out_6), .out_7(control_unit_1_out_7), .out_8(control_unit_1_out_8),
    .out_9(control_unit_1_out_9), .out_10(control_unit_1_out_10), .out_11(control_unit_1_out_11),
    .out_12(control_unit_1_out_12), .in_2(rom_1_data[14:12]), .in_3(rom_1_data[30]));
  branch a (
    .in_1(register_file_circ_1_out_7), .in_2(register_file_circ_1_out_8), .in_3(rom_1_data[14:12]),
    .out_5(a_out_5), .in_4(control_unit_1_out_7));
  Multiplexer #(.select(2), .width(32)) multiplexer_3 (
    .in1(immediate_generation_1_out_7), .in2(immediate_generation_1_out_3),
    .in3(immediate_generation_1_out_4), .out(multiplexer_3_out), .sel(control_unit_1_out_12));  // open: in0, en
  alu alu_1 (
    .in_1(multiplexer_5_out), .in_2(multiplexer_4_out), .in_3(control_unit_1_out_11),
    .out_4({alu_1_out_4[31:14], alu_1_out_4_2, alu_1_out_4[1:0]}));
  Multiplexer #(.select(2), .width(32), .enable("false")) multiplexer_4 (
    .in0(register_file_circ_1_out_7), .in1(register_1_q), .in2(adder_2_out), .in3({32{1'b0}}),
    .out(multiplexer_4_out), .sel(control_unit_1_out_8));
  Multiplexer #(.width(32), .enable("false")) multiplexer_5 (
    .in0(register_file_circ_1_out_8), .in1(multiplexer_3_out), .out(multiplexer_5_out),
    .sel(control_unit_1_out_9));
  RAM #(.addrWidth(12), .dataWidth(32), .bus("separate")) ram_1 (
    .addr(alu_1_out_4_2), .din(register_file_circ_1_out_8), .data(ram_1_data), .str(control_unit_1_out_6),
    .clk(clock_1_out), .ld(control_unit_1_out_5));  // open: sel, clr
  Multiplexer #(.width(32), .enable("false")) multiplexer_6 (
    .in0({alu_1_out_4[31:14], alu_1_out_4_2, alu_1_out_4[1:0]}), .in1(ram_1_data), .out(multiplexer_6_out),
    .sel(control_unit_1_out_5));

  // Notes on the sheet:
  //   RV32I SINGLE_CYCLE PROCESSOR
  //   contents of rom_1 (hex, n*v repeats v):
  //   200093 1080b3 108133
  //   CLOCK
  //   MUHAMMAD TALHA
  //   21B-099-CE
endmodule

module operand_a_circ (
  input  AUIPC,
  input  JAL,
  input  JALR,
  input  LUI,
  input  RS1,
  output a,
  output b
);

  or or_1 (a, LUI, JAL, AUIPC);
  or or_2 (b, LUI, JALR);
endmodule

module operand_A_circ (
  input  AUIPC,
  input  JAL,
  input  JALR,
  input  LUI,
  input  RS1,
  output a,
  output b
);

  or or_1 (a, LUI, AUIPC);
  or or_2 (b, LUI, JALR, JAL);
endmodule
